# Fritzing sketch aqi_led (saved by Fritzing 0.9.3b)
breadboards: 1

parts:
  Raspberry_Pi1 = Raspberry Pi 2
  LED2 = smd LED [color="Red (633nm)" package="0603 [SMD]"]
  LED3 = smd LED [color="Red (633nm)" package="0603 [SMD]"]
  LED4 = smd LED [color="Red (633nm)" package="0603 [SMD]"]
  LED5 = smd LED [color="Red (633nm)" package="0603 [SMD]"]
  R1 = Resistor [tolerance=±5% resistance=220 package="2010 [SMD]"]
  R2 = Resistor [tolerance=±5% resistance=220 package="2010 [SMD]"]
  R3 = Resistor [tolerance=±5% resistance=220 package="2010 [SMD]"]
  R4 = Resistor [tolerance=±5% resistance=220 package="2010 [SMD]"]
  R5 = Resistor [tolerance=±5% resistance=220 package="2010 [SMD]"]
  R6 = Resistor [tolerance=±5% resistance=220 package="2010 [SMD]"]
  LED8 = LED - 3mm [color="Red (633nm)" package="3 mm [THT]"]
  LED9 = LED - 3mm [color="Green (555nm)" package="3 mm [THT]"]

nets:
  N1: Raspberry_Pi1.GND, R1.Pin_1, R2.Pin_1, R3.Pin_1, R4.Pin_1, R5.Pin_1, R6.Pin_1
  N2: Raspberry_Pi1.GPIO20, LED9.anode
  N3: Raspberry_Pi1.GPIO16, LED5.anode
  N4: Raspberry_Pi1.GPIO12, LED4.anode
  N5: Raspberry_Pi1.GPIO25, LED3.anode
  N6: Raspberry_Pi1.GPIO24, LED2.anode
  N7: Raspberry_Pi1.GPIO23, LED8.anode
  N8: LED2.cathode, R2.Pin_0
  N9: LED3.cathode, R3.Pin_0
  N10: LED4.cathode, R4.Pin_0
  N11: LED5.cathode, R5.Pin_0
  N12: R1.Pin_0, LED8.cathode
  N13: R6.Pin_0, LED9.cathode
